# Fritzing sketch esp8266_sensors (saved by Fritzing 0.9.2b)
circuit board: 8.46667cm x 5.64444cm
perfboards: 1

parts:
  RHT1 = Humidity and Temperature Sensor RHT03
  J1 = female pin header, 11 pins [form="♀ (female)"]
  MOD-WIFI-ESP8266-DEV1 = Olimex ESP8266 DEV
  J2 = female pin header, 11 pins [form="♀ (female)"]
  J3 = Screw terminal - 2 pins [package=THT]
  J5 = male pin header, 2 pins [form="♂ (male)"]
  J4 = female pin header, 6 pins [form="♀ (female)"]
  R1 = Resistor [tolerance=±5% resistance=10k package=THT]
  S2 = Pushbutton [package="[THT]"]
  IC1 = Voltage Regulator [package=to-92]
  C1 = Tantalum Capacitor [capacitance="1 μF" package="100 mil [THT, tantalum]"]
  C2 = Tantalum Capacitor [capacitance="1 μF" package="100 mil [THT, tantalum]"]

nets:
  VCC: RHT1.Vcc, J1.pin1, MOD-WIFI-ESP8266-DEV1.3.3V, R1.Pin_1, IC1.OUT, C2.+
  GND: RHT1.GND_2, J1.pin2, MOD-WIFI-ESP8266-DEV1.GND, J3.pin1, J4.pin1, S2.Pin_1, S2.Pin_2, IC1.GND, C1.-, C2.-
  N1: J1.pin3, MOD-WIFI-ESP8266-DEV1.GPIO1, J4.pin5
  N2: J1.pin4, MOD-WIFI-ESP8266-DEV1.GPIO3, J4.pin4
  N3: J1.pin5, MOD-WIFI-ESP8266-DEV1.SD_CLK
  N4: J1.pin6, MOD-WIFI-ESP8266-DEV1.SD_D2
  N5: J1.pin7, MOD-WIFI-ESP8266-DEV1.SD_D1
  N6: J1.pin8, MOD-WIFI-ESP8266-DEV1.SD_CMD
  N7: J1.pin9, MOD-WIFI-ESP8266-DEV1.SD_D0
  N8: J1.pin10, MOD-WIFI-ESP8266-DEV1.SD_D3
  N9: J1.pin11, MOD-WIFI-ESP8266-DEV1.GPIO5
  N10: MOD-WIFI-ESP8266-DEV1.ADC, J2.pin11
  N11: MOD-WIFI-ESP8266-DEV1.RSTB, J2.pin10, J5.pin2, S2.Pin_3, S2.Pin_4
  N12: MOD-WIFI-ESP8266-DEV1.CHIP_E, J2.pin9
  N13: MOD-WIFI-ESP8266-DEV1.GPIO16, J2.pin8, J5.pin1
  N14: MOD-WIFI-ESP8266-DEV1.GPIO12, J2.pin7
  N15: MOD-WIFI-ESP8266-DEV1.GPIO14, J2.pin6
  N16: MOD-WIFI-ESP8266-DEV1.GPIO13, J2.pin5
  N17: MOD-WIFI-ESP8266-DEV1.GPIO15, J2.pin4
  N18: MOD-WIFI-ESP8266-DEV1.GPIO2, J2.pin3
  N19: MOD-WIFI-ESP8266-DEV1.GPIO0, J2.pin2
  N20: MOD-WIFI-ESP8266-DEV1.GPIO4, J2.pin1
  N21: IC1.IN, C1.+

notes:
  GND
  CTS
  POWER
  TXO
  RXI
  DTR
  GPIO1: U0TXD -> RXI
  GPIO3: U0RXD -> TXO
  RESET
  IC1: MCP1700-3302E/TO
  C1 and C2: 2.2µF

custom parts:
  Olimex ESP8266 DEV: MOD-WIFI-ESP8266-DEV is the ultimate development board for ESP8266 with all GPIOs and resources exposed, can be soldered to PCB or used with breadboard and UEXT. Small U.FL connector is provided for external antenna connection. ESP8266 is very highly integrated SOC which includes Xtensa LX106 core processor, RAM, RF front end and allow WIFI TCP-IP stack to be implemented on board with just few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
